# Fritzing sketch thermostat_universal (saved by Fritzing 1.0.1)

parts:
  J1 = JST XH 3-pin B3B-XH-A [package=THT]
  J2 = JST XH 4-pin B4B-XH-A [package=THT]
  J3 = JST XH 4-pin B4B-XH-A [package=THT]
  J4 = JST XH 4-pin B4B-XH-A [package=THT]
  J5 = JST XH 4-pin B4B-XH-A [package=THT]
  J6 = JST XH 4-pin B4B-XH-A [package=THT]
  J7 = JST XH 4-pin B4B-XH-A [package=THT]
  J8 = JST XH 3-pin B3B-XH-A [package=THT]
  J9 = JST XH 3-pin B3B-XH-A [package=THT]
  J10 = JST XH 5-pin B5B-XH-A [package=THT]
  F1 = Resettable Fuse PTC [package=ptc]
  C7 = Ceramic Capacitor [capacitance="100 nF" package="100 mil [THT, multilayer]"]
  C8 = Electrolytic Capacitor [capacitance="100 uF" voltage=10V package="100 mil [THT, electrolytic]"]
  C9 = Ceramic Capacitor [capacitance="100 nF" package="100 mil [THT, multilayer]"]
  C10 = Electrolytic Capacitor [capacitance="47 uF" voltage=10V package="100 mil [THT, electrolytic]"]
  R7 = Resistor [resistance=4.7k package=THT]
  R8 = Resistor [resistance=4.7k package=THT]
  R9 = Resistor [resistance=4.7k package=THT]
  R10 = Resistor [resistance=0 package=THT]
  R11 = Resistor [resistance=0 package=THT]
  R12 = Resistor [resistance=0 package=THT]
  R13 = Resistor [resistance=0 package=THT]
  R14 = Resistor [resistance=0 package=THT]
  R15 = Resistor [resistance=10k package=THT]
  R16 = Resistor [resistance=10k package=THT]
  R17 = Resistor [resistance=10k package=THT]
  R1 = Resistor [resistance=1k package=THT]
  R2 = Resistor [resistance=10k package=THT]
  Q1 = BC547B C-B-E straight 2.54 mm [package="TO-92 THT"]
  C1 = Ceramic Capacitor [capacitance="100 nF" package="100 mil [THT, multilayer]"]
  J11 = MKDS 1,5/2-5,08 1715721 [package=THT]
  R3 = Resistor [resistance=1k package=THT]
  R4 = Resistor [resistance=10k package=THT]
  Q2 = BC547B C-B-E straight 2.54 mm [package="TO-92 THT"]
  C2 = Ceramic Capacitor [capacitance="100 nF" package="100 mil [THT, multilayer]"]
  J12 = MKDS 1,5/2-5,08 1715721 [package=THT]
  R5 = Resistor [resistance=1k package=THT]
  R6 = Resistor [resistance=10k package=THT]
  Q3 = BC547B C-B-E straight 2.54 mm [package="TO-92 THT"]
  C3 = Ceramic Capacitor [capacitance="100 nF" package="100 mil [THT, multilayer]"]
  J13 = MKDS 1,5/2-5,08 1715721 [package=THT]
  H1 = Mounting hole NPTH 3 mm [package="NPTH 3mm"]  # not connected
  H2 = Mounting hole NPTH 3 mm [package="NPTH 3mm"]  # not connected
  H3 = Mounting hole NPTH 3 mm [package="NPTH 3mm"]  # not connected
  H4 = Mounting hole NPTH 3 mm [package="NPTH 3mm"]  # not connected
  VIA_D7_COMP_8000 = Plated via 1.4/0.6 mm [package=THT]  # not connected
  VIA_GND_ENTRY_8001 = Plated via 1.4/0.6 mm [package=THT]  # not connected
  VIA_GND_ENTRY_8002 = Plated via 1.4/0.6 mm [package=THT]  # not connected
  VIA_GND_ENTRY_8003 = Plated via 1.4/0.6 mm [package=THT]  # not connected
  VIA_GND_LOGIC_8004 = Plated via 1.4/0.6 mm [package=THT]  # not connected
  VIA_GND_LOGIC_8005 = Plated via 1.4/0.6 mm [package=THT]  # not connected
  VIA_GND_LOGIC_8006 = Plated via 1.4/0.6 mm [package=THT]  # not connected
  VIA_3V3_ENTRY_8007 = Plated via 1.4/0.6 mm [package=THT]  # not connected
  VIA_3V3_ENTRY_8008 = Plated via 1.4/0.6 mm [package=THT]  # not connected
  VIA_3V3_ENTRY_8009 = Plated via 1.4/0.6 mm [package=THT]  # not connected
  VIA_3V3_ENTRY_8010 = Plated via 1.4/0.6 mm [package=THT]  # not connected
  VIA_3V3_ENTRY_8011 = Plated via 1.4/0.6 mm [package=THT]  # not connected
  VIA_3V3_ENTRY_8012 = Plated via 1.4/0.6 mm [package=THT]  # not connected
  VIA_3V3_I2C_8013 = Plated via 1.4/0.6 mm [package=THT]  # not connected
  VIA_5V_SSR_8014 = Plated via 1.4/0.6 mm [package=THT]  # not connected
  VIA_5V_SSR_8015 = Plated via 1.4/0.6 mm [package=THT]  # not connected
  VIA_5V_SSR_8016 = Plated via 1.4/0.6 mm [package=THT]  # not connected
  VIA_5V_SSR_8017 = Plated via 1.4/0.6 mm [package=THT]  # not connected

nets:
  N1: J1.1, F1.1
  N2: J1.2, C9.0, C10.+, R13.Pin_0, R14.Pin_0
  N3: J1.3, C7.1, C8.-, C9.1, C10.-, R10.Pin_0, R11.Pin_0
  N4: J2.1, R5.Pin_0
  N5: J2.2, R3.Pin_0
  N6: J2.3, R1.Pin_0
  N7: J2.4, J8.2, R9.Pin_0
  N8: J3.1, J5.3, J6.3, J7.3, R8.Pin_0
  N9: J3.2, J5.4, J6.4, J7.4, R7.Pin_0
  N10: J3.3, J9.2
  N11: J3.4, J4.4, J8.3, J9.3, J10.4, R11.Pin_1, R12.Pin_0, R15.Pin_1
  N12: J4.1, J10.1, R15.Pin_0
  N13: J4.2, J10.2, R16.Pin_0
  N14: J4.3, J10.3, R17.Pin_0
  N15: J5.1, J6.1, J7.1, J10.5, R7.Pin_1, R8.Pin_1, R13.Pin_1, R16.Pin_1, R17.Pin_1
  N16: J5.2, J6.2, J7.2, R12.Pin_1
  N17: J8.1, J9.1, R9.Pin_1, R14.Pin_1
  N18: F1.2, C7.0, C8.+, C1.0, J11.1, C2.0, J12.1, C3.0, J13.1
  N19: R10.Pin_1, R2.Pin_1, Q1.E, R4.Pin_1, Q2.E, R6.Pin_1, Q3.E
  N20: R1.Pin_1, R2.Pin_0, Q1.B
  N21: Q1.C, C1.1, J11.2
  N22: R3.Pin_1, R4.Pin_0, Q2.B
  N23: Q2.C, C2.1, J12.2
  N24: R5.Pin_1, R6.Pin_0, Q3.B
  N25: Q3.C, C3.1, J13.2

custom parts:
  JST XH 3-pin B3B-XH-A: JST XH top-entry, 2.50 mm pitch, 0.90 mm drill.
  JST XH 4-pin B4B-XH-A: JST XH top-entry, 2.50 mm pitch, 0.90 mm drill.
  JST XH 5-pin B5B-XH-A: JST XH top-entry, 2.50 mm pitch, 0.90 mm drill.
  BC547B C-B-E straight 2.54 mm: Diotec BC547B TO-92 straight C-B-E, 2.54 mm pitch, flat side on marked edge.
  MKDS 1,5/2-5,08 1715721: Phoenix Contact 1715721, 5.08 mm pitch, 1.30 mm drill.
  Mounting hole NPTH 3 mm: Unplated 3.0 mm mounting hole; 7 mm copper/component keepout.
  Plated via 1.4/0.6 mm: Two-layer plated through via.
