# Fritzing sketch sketch (saved by Fritzing 0.9.3b)

parts:
  U1 = ESP8266 NodeMCU LoLin module
  DHT1 = DHT22 Humidity and Temperature Sensor
  Grove1 = Grove OLED 128x96
  Grove2 = Grove OLED 128x96
  Componente1 = Real Time Clock Module - DS1307 RTC Breakout Board
  S3 = Toggle Switch [package=THT]
  U2 = POT [package=3362u]
  S2 = SWITCH-MOMENTARY-2 [package=tactile-switch-1101ne]
  S1 = SWITCH-MOMENTARY-2 [package=tactile-switch-1101ne]
  U3 = RELAY-SOLIDSTATE [package=relay-s108t02]
  U4 = RELAY-SOLIDSTATE [package=relay-s108t02]
  U5 = RELAY-SOLIDSTATE [package=relay-s108t02]

nets:
  N1: U1.D0, S3.COM
  N2: U1.D1, Grove1.SCL, Grove2.SCL, Componente1.SCL
  N3: U1.D2, Grove1.SDA, Grove2.SDA, Componente1.SDA
  N4: U1.D3, S2.2
  N5: U1.D4, S1.2
  VCC: U1.3V3, DHT1.VDD, Grove1.VCC, Grove2.VCC, Componente1.5V, S3.L2, U2.A
  GND: U1.GND, DHT1.GND, Grove1.GND, Grove2.GND, Componente1.GND, S3.L1, U2.E, U3.-, U4.-, U5.-
  N6: U1.D5, DHT1.DATA
  N7: U1.D6, U5.+
  N8: U1.D7, U3.+
  N9: U1.D8, U4.+
  N10: U1.A0, U2.S

custom parts:
  ESP8266 NodeMCU LoLin module: ESP8266 based NodeMCU
