# Fritzing sketch sketch_pcb (saved by Fritzing 0.9.3b)

parts:
  U1 = ESP8266 NodeMCU LoLin module
  DHT1 = DHT22 Humidity and Temperature Sensor
  Grove1 = Grove OLED 128x96
  Grove2 = Grove OLED 128x96
  Componente1 = Real Time Clock Module - DS1307 RTC Breakout Board
  S3 = Toggle Switch [package=THT]
  U2 = POT [package=3362u]
  S2 = SWITCH-MOMENTARY-2 [package=tactile-switch-1101ne]
  S1 = SWITCH-MOMENTARY-2 [package=tactile-switch-1101ne]
  J_COMPRESSOR_SSR_5V = Screw terminal - 2 pins [package=THT]
  J_HEATING_SSR_5V = Screw terminal - 2 pins [package=THT]
  J_FAN_SSR_5V = Screw terminal - 2 pins [package=THT]
  1k_COMPRESSOR = 220 Ω Resistor [package=THT]
  10k_COMPRESSOR = 220 Ω Resistor [package=THT]
  Q_COMPRESSOR_BC547B_CBE = TRANSISTOR_NPN_2 [package=to-92]
  100nF_SSR_COMPRESSOR = Ceramic Capacitor [package="100 mil [THT, multilayer]"]
  1k_HEATING = 220 Ω Resistor [package=THT]
  10k_HEATING = 220 Ω Resistor [package=THT]
  Q_HEATING_BC547B_CBE = TRANSISTOR_NPN_2 [package=to-92]
  100nF_SSR_HEATING = Ceramic Capacitor [package="100 mil [THT, multilayer]"]
  1k_FAN = 220 Ω Resistor [package=THT]
  10k_FAN = 220 Ω Resistor [package=THT]
  Q_FAN_BC547B_CBE = TRANSISTOR_NPN_2 [package=to-92]
  100nF_SSR_FAN = Ceramic Capacitor [package="100 mil [THT, multilayer]"]
  100nF_ESP8266 = Ceramic Capacitor [package="100 mil [THT, multilayer]"]
  100nF_OLED_A = Ceramic Capacitor [package="100 mil [THT, multilayer]"]
  100nF_OLED_B = Ceramic Capacitor [package="100 mil [THT, multilayer]"]
  100nF_RTC = Ceramic Capacitor [package="100 mil [THT, multilayer]"]
  100nF_DHT22 = Ceramic Capacitor [package="100 mil [THT, multilayer]"]
  100uF_bulk_3V3 = Electrolytic Capacitor [package="100 mil [THT, electrolytic]"]
  4_7k_SDA_OPTIONAL_DNP = 220 Ω Resistor [package=THT]
  4_7k_SCL_OPTIONAL_DNP = 220 Ω Resistor [package=THT]

nets:
  N1: U1.D0, S3.COM
  N2: U1.D1, Grove1.SCL, Grove2.SCL, Componente1.SCL, 4_7k_SCL_OPTIONAL_DNP.Pin_0
  N3: U1.D2, Grove1.SDA, Grove2.SDA, Componente1.SDA, 4_7k_SDA_OPTIONAL_DNP.Pin_0
  N4: U1.D3, S2.2
  N5: U1.D4, S1.2
  VCC: U1.3V3, DHT1.VDD, Grove1.VCC, Grove2.VCC, Componente1.5V, S3.L2, U2.A, 100nF_ESP8266.0, 100nF_OLED_A.0, 100nF_OLED_B.0, 100nF_RTC.0, 100nF_DHT22.0, 100uF_bulk_3V3.+, 4_7k_SDA_OPTIONAL_DNP.Pin_1, 4_7k_SCL_OPTIONAL_DNP.Pin_1
  GND: U1.GND, DHT1.GND, Grove1.GND, Grove2.GND, Componente1.GND, S3.L1, U2.E, 10k_COMPRESSOR.Pin_1, Q_COMPRESSOR_BC547B_CBE.E, 10k_HEATING.Pin_1, Q_HEATING_BC547B_CBE.E, 10k_FAN.Pin_1, Q_FAN_BC547B_CBE.E, 100nF_ESP8266.1, 100nF_OLED_A.1, 100nF_OLED_B.1, 100nF_RTC.1, 100nF_DHT22.1, 100uF_bulk_3V3.-
  N6: U1.D5, DHT1.DATA
  N7: U1.D6, 1k_FAN.Pin_0
  N8: U1.D7, 1k_COMPRESSOR.Pin_0
  N9: U1.D8, 1k_HEATING.Pin_0
  N10: U1.Vin, J_COMPRESSOR_SSR_5V.pin1, J_HEATING_SSR_5V.pin1, J_FAN_SSR_5V.pin1, 100nF_SSR_COMPRESSOR.1, 100nF_SSR_HEATING.1, 100nF_SSR_FAN.1
  N11: U1.A0, U2.S
  N12: J_COMPRESSOR_SSR_5V.pin2, Q_COMPRESSOR_BC547B_CBE.C, 100nF_SSR_COMPRESSOR.0
  N13: J_HEATING_SSR_5V.pin2, Q_HEATING_BC547B_CBE.C, 100nF_SSR_HEATING.0
  N14: J_FAN_SSR_5V.pin2, Q_FAN_BC547B_CBE.C, 100nF_SSR_FAN.0
  N15: 1k_COMPRESSOR.Pin_1, 10k_COMPRESSOR.Pin_0, Q_COMPRESSOR_BC547B_CBE.B
  N16: 1k_HEATING.Pin_1, 10k_HEATING.Pin_0, Q_HEATING_BC547B_CBE.B
  N17: 1k_FAN.Pin_1, 10k_FAN.Pin_0, Q_FAN_BC547B_CBE.B

custom parts:
  ESP8266 NodeMCU LoLin module: ESP8266 based NodeMCU
