# Fritzing sketch thermostat_rev_b (saved by Fritzing 1.0.1)
circuit board: 84.0mm x 84.0mm

parts:
  J20 = Screw terminal 4P 5.08 mm [value="MKDS 4P 230V" package=THT]
  F2 = TR5 fuse 5.08 mm [value="T6.3A 250V" package=THT]
  RL1 = Hongfa HF115F/005-1ZS3 (16 A, 5 mm pinning) [value="HF115F 5V COMP" package=THT]
  RL2 = Hongfa HF115F/005-1ZS3 (16 A, 5 mm pinning) [value="HF115F 5V HEAT" package=THT]
  RL3 = Hongfa HF115F/005-1ZS3 (16 A, 5 mm pinning) [value="HF115F 5V FAN" package=THT]
  U1 = NodeMCU socket, 0.9" and 1.1" rows [value="NodeMCU ESP8266" package=THT]
  R1 = 0805 res [value=1k package=SMD]
  R2 = 0805 res [value=10k package=SMD]
  Q1 = BC817-40 SOT-23 (1=B 2=E 3=C) [value=BC817-40 package=SMD]
  D1 = 1N4148W SOD-123 (cathode bar = pad 1) [value=1N4148W package=SMD]
  R3 = 0805 res [value=1k package=SMD]
  R4 = 0805 res [value=10k package=SMD]
  Q2 = BC817-40 SOT-23 (1=B 2=E 3=C) [value=BC817-40 package=SMD]
  D2 = 1N4148W SOD-123 (cathode bar = pad 1) [value=1N4148W package=SMD]
  R5 = 0805 res [value=1k package=SMD]
  R6 = 0805 res [value=10k package=SMD]
  Q3 = BC817-40 SOT-23 (1=B 2=E 3=C) [value=BC817-40 package=SMD]
  D3 = 1N4148W SOD-123 (cathode bar = pad 1) [value=1N4148W package=SMD]
  J1 = Screw terminal 2P 5.08 mm [value="5V IN" package=THT]
  F1 = PTC 1812 [value="1.1A PTC" package=SMD]
  C1 = Electrolytic 6.3 mm, 2.5 mm pitch [value="220uF 16V" package=THT]
  C2 = 0805 cap [value=100nF package=SMD]
  J2 = JST XH 4P B4B-XH-A [value="DWIN UART" package=THT]
  J5 = JST XH 4P B4B-XH-A [value="RTC I2C" package=THT]
  J3 = JST XH 3P B3B-XH-A [value=DHT22 package=THT]
  J4 = JST XH 2P B2B-XH-A [value=ON/OFF package=THT]
  C3 = 0805 cap [value=100nF package=SMD]
  R16 = 0805 res [value=10k package=SMD]
  R18 = 0805 res [value=1k package=SMD]
  R17 = 0805 res [value=10k package=SMD]
  R19 = 0805 res [value=1k package=SMD]
  R15 = 0805 res [value=10k package=SMD]
  R9 = 0805 res [value=10k package=SMD]
  H1 = Mounting hole NPTH 3.2 mm [package=NPTH]  # not connected
  H2 = Mounting hole NPTH 3.2 mm [package=NPTH]  # not connected
  H3 = Mounting hole NPTH 3.2 mm [package=NPTH]  # not connected
  H4 = Mounting hole NPTH 3.2 mm [package=NPTH]  # not connected
  LEGEND = Rev B board legend  # not connected
  VIA_BASE_HEAT = Plated via 1.4/0.6 mm [package=THT]
  VIA_BASE_HEAT_2 = Plated via 1.4/0.6 mm [package=THT]
  VIA_BASE_FAN = Plated via 1.4/0.6 mm [package=THT]
  VIA_BASE_FAN_2 = Plated via 1.4/0.6 mm [package=THT]
  VIA_BASE_FAN_3 = Plated via 1.4/0.6 mm [package=THT]
  VIA_D5_DHT = Plated via 1.4/0.6 mm [package=THT]
  VIA_D0_ONOFF = Plated via 1.4/0.6 mm [package=THT]
  VIA_D0_ONOFF_2 = Plated via 1.4/0.6 mm [package=THT]
  VIA_D8_HEAT = Plated via 1.4/0.6 mm [package=THT]
  VIA_DWIN_TX = Plated via 1.4/0.6 mm [package=THT]
  VIA_3V3 = Plated via 1.4/0.6 mm [package=THT]
  VIA_3V3_2 = Plated via 1.4/0.6 mm [package=THT]
  VIA_3V3_3 = Plated via 1.4/0.6 mm [package=THT]
  VIA_3V3_4 = Plated via 1.4/0.6 mm [package=THT]
  VIA_D3_RXD = Plated via 1.4/0.6 mm [package=THT]
  VIA_D3_RXD_2 = Plated via 1.4/0.6 mm [package=THT]
  VIA_D3_RXD_3 = Plated via 1.4/0.6 mm [package=THT]
  VIA_D3_RXD_4 = Plated via 1.4/0.6 mm [package=THT]
  VIA_D6_FAN = Plated via 1.4/0.6 mm [package=THT]
  VIA_BASE_COMP = Plated via 1.4/0.6 mm [package=THT]
  VIA_BASE_COMP_2 = Plated via 1.4/0.6 mm [package=THT]
  VIA_COIL_HEAT = Plated via 1.4/0.6 mm [package=THT]
  VIA_COIL_FAN = Plated via 1.4/0.6 mm [package=THT]
  VIA_DWIN_RX = Plated via 1.4/0.6 mm [package=THT]
  VIA_5V_IN = Plated via 1.4/0.6 mm [package=THT]
  VIA_5V = Plated via 1.4/0.6 mm [package=THT]
  VIA_5V_2 = Plated via 1.4/0.6 mm [package=THT]

nets:
  L_IN: J20.L, F2.2
  OUT_COMP: J20.COMP, RL1.NO, RL1.NO'
  OUT_HEAT: J20.CALOR, RL2.NO, RL2.NO'
  OUT_FAN: J20.VENT, RL3.NO, RL3.NO'
  L_FUSED: F2.1, RL1.COM, RL1.COM', RL2.COM, RL2.COM', RL3.COM, RL3.COM'
  +5V: RL1.A1, RL2.A1, RL3.A1, U1.T00_VIN, U1.T00_VIN', D1.K, D2.K, D3.K, F1.2, C1.+, C2.1, J2.+5V, VIA_5V.via, VIA_5V_2.via
  COIL_COMP: RL1.A2, Q1.C, D1.A
  N1: RL1.NC, RL1.NC'
  COIL_HEAT: RL2.A2, Q2.C, D2.A, VIA_COIL_HEAT.via
  N2: RL2.NC, RL2.NC'
  COIL_FAN: RL3.A2, Q3.C, D3.A, VIA_COIL_FAN.via
  N3: RL3.NC, RL3.NC'
  GND: U1.T01_GND, U1.T01_GND', U1.B08_GND, U1.B08_GND', R2.2, Q1.E, R4.2, Q2.E, R6.2, Q3.E, J1.GND, C1.-, C2.2, J2.GND, J5.GND, J3.GND, C3.2, R15.2
  N4: U1.T02_RST, U1.T02_RST'
  N5: U1.T03_EN, U1.T03_EN'
  N6: U1.T04_3V3, U1.T04_3V3'
  N7: U1.T05_GND, U1.T05_GND'
  N8: U1.T06_CLK, U1.T06_CLK'
  N9: U1.T07_SD0, U1.T07_SD0'
  N10: U1.T08_CMD, U1.T08_CMD'
  N11: U1.T09_SD1, U1.T09_SD1'
  N12: U1.T10_SD2, U1.T10_SD2'
  N13: U1.T11_SD3, U1.T11_SD3'
  N14: U1.T12_RSV, U1.T12_RSV'
  N15: U1.T13_RSV, U1.T13_RSV'
  N16: U1.T14_A0, U1.T14_A0'
  N17: U1.B00_3V3, U1.B00_3V3'
  N18: U1.B01_GND, U1.B01_GND'
  N19: U1.B02_TX, U1.B02_TX'
  N20: U1.B03_RX, U1.B03_RX'
  D8_HEAT: U1.B04_D8, U1.B04_D8', R3.1, VIA_D8_HEAT.via
  D7_COMP: U1.B05_D7, U1.B05_D7', R1.1
  D6_FAN: U1.B06_D6, U1.B06_D6', R5.1, VIA_D6_FAN.via
  D5_DHT: U1.B07_D5, U1.B07_D5', J3.DATA, R9.1, VIA_D5_DHT.via
  +3V3: U1.B09_3V3, U1.B09_3V3', J5.3V3, J3.3V3, J4.3V3, C3.1, R16.2, R17.2, R9.2, VIA_3V3.via, VIA_3V3_2.via, VIA_3V3_3.via, VIA_3V3_4.via
  D4_TXD: U1.B10_D4, U1.B10_D4', R17.1, R19.1
  D3_RXD: U1.B11_D3, U1.B11_D3', R16.1, R18.1, VIA_D3_RXD.via, VIA_D3_RXD_2.via, VIA_D3_RXD_3.via, VIA_D3_RXD_4.via
  D2_SDA: U1.B12_D2, U1.B12_D2', J5.SDA
  D1_SCL: U1.B13_D1, U1.B13_D1', J5.SCL
  D0_ONOFF: U1.B14_D0, U1.B14_D0', J4.D0, R15.1, VIA_D0_ONOFF.via, VIA_D0_ONOFF_2.via
  BASE_COMP: R1.2, R2.1, Q1.B, VIA_BASE_COMP.via, VIA_BASE_COMP_2.via
  BASE_HEAT: R3.2, R4.1, Q2.B, VIA_BASE_HEAT.via, VIA_BASE_HEAT_2.via
  BASE_FAN: R5.2, R6.1, Q3.B, VIA_BASE_FAN.via, VIA_BASE_FAN_2.via, VIA_BASE_FAN_3.via
  +5V_IN: J1.+5V, F1.1, VIA_5V_IN.via
  DWIN_TX: J2.TX, R18.2, VIA_DWIN_TX.via
  DWIN_RX: J2.RX, R19.2, VIA_DWIN_RX.via

custom parts:
  Screw terminal 4P 5.08 mm: Phoenix MKDS 1,5 family, 1.30 mm drill
  TR5 fuse 5.08 mm: Radial TR5 fuse, 8.5 mm body
  Hongfa HF115F/005-1ZS3 (16 A, 5 mm pinning): SPDT 16 A 250 VAC relay, 5 V coil, 29 x 12.7 x 15.7 mm
  NodeMCU socket, 0.9" and 1.1" rows: Two 1x15 female headers; outer rows = LoLin v3 (27.94 mm), inner rows = Amica v2 (22.86 mm)
  0805 res: SMD 0805
  BC817-40 SOT-23 (1=B 2=E 3=C): SOT-23 NPN
  1N4148W SOD-123 (cathode bar = pad 1): SOD-123 diode
  Screw terminal 2P 5.08 mm: Phoenix MKDS 1,5 family, 1.30 mm drill
  PTC 1812: SMD 1812 polyfuse
  Electrolytic 6.3 mm, 2.5 mm pitch: Radial electrolytic
  0805 cap: SMD 0805
  JST XH 4P B4B-XH-A: JST XH top entry, 2.50 mm, 0.90 mm drill
  JST XH 4P B4B-XH-A: JST XH top entry, 2.50 mm, 0.90 mm drill
  JST XH 3P B3B-XH-A: JST XH top entry, 2.50 mm, 0.90 mm drill
  JST XH 2P B2B-XH-A: JST XH top entry, 2.50 mm, 0.90 mm drill
  Mounting hole NPTH 3.2 mm: Unplated mounting hole; use nylon M3 screws.
  Rev B board legend: Board-level silkscreen legend.
  Plated via 1.4/0.6 mm: Two-layer plated through via.
