# Fritzing sketch thermostat_rev_c (saved by Fritzing 1.0.1)
circuit board: 84.0mm x 84.0mm

parts:
  J20 = Screw terminal 4P 5.08 mm [value="MKDS 4P 230V" package=THT]
  F2 = TR5 fuse 5.08 mm [value="T6.3A 250V" package=THT]
  RL1 = Hongfa HF115F/005-1ZS3 (16 A, 5 mm pinning) [value="HF115F 5V COMP" package=THT]
  RL2 = Hongfa HF115F/005-1ZS3 (16 A, 5 mm pinning) [value="HF115F 5V FAN" package=THT]
  RL3 = Hongfa HF115F/005-1ZS3 (16 A, 5 mm pinning) [value="HF115F 5V HEAT" package=THT]
  U1 = NodeMCU Amica v2 socket (22.86 mm rows) [value="NodeMCU Amica" package=THT]
  J6 = FPC 0.5 mm 50P upper contact (AFC07-S50ECA-00), bottom side [value="DWIN FPC50" package=SMD]
  R1 = 0805 res [value=1k package=SMD]
  R2 = 0805 res [value=10k package=SMD]
  Q1 = BC817-40 SOT-23 (1=B 2=E 3=C) [value=BC817-40 package=SMD]
  D1 = 1N4148W SOD-123 (cathode bar = pad 1) [value=1N4148W package=SMD]
  R3 = 0805 res [value=1k package=SMD]
  R4 = 0805 res [value=10k package=SMD]
  Q2 = BC817-40 SOT-23 (1=B 2=E 3=C) [value=BC817-40 package=SMD]
  D2 = 1N4148W SOD-123 (cathode bar = pad 1) [value=1N4148W package=SMD]
  R5 = 0805 res [value=1k package=SMD]
  R6 = 0805 res [value=10k package=SMD]
  Q3 = BC817-40 SOT-23 (1=B 2=E 3=C) [value=BC817-40 package=SMD]
  D3 = 1N4148W SOD-123 (cathode bar = pad 1) [value=1N4148W package=SMD]
  J1 = Screw terminal 2P 5.08 mm [value="5V IN" package=THT]
  F1 = PTC 1812 [value="1.1A PTC" package=SMD]
  C1 = Electrolytic 6.3 mm, 2.5 mm pitch [value="220uF 16V" package=THT]
  C2 = 0805 cap [value=100nF package=SMD]
  J5 = JST XH 4P B4B-XH-A [value="RTC I2C" package=THT]
  J3 = JST XH 4P B4B-XH-A [value=SHT40 package=THT]
  C3 = 0805 cap [value=100nF package=SMD]
  R16 = 0805 res [value=10k package=SMD]
  R18 = 0805 res [value=1k package=SMD]
  R17 = 0805 res [value=10k package=SMD]
  R19 = 0805 res [value=1k package=SMD]
  H1 = Mounting hole NPTH 3.2 mm [package=NPTH]  # not connected
  H2 = Mounting hole NPTH 3.2 mm [package=NPTH]  # not connected
  H3 = Mounting hole NPTH 3.2 mm [package=NPTH]  # not connected
  H4 = Mounting hole NPTH 3.2 mm [package=NPTH]  # not connected
  LEGEND = Rev B board legend  # not connected
  VIA_GND = Plated via 1.4/0.6 mm [package=THT]
  VIA_GND_2 = Plated via 1.4/0.6 mm [package=THT]
  VIA_COIL_COMP = Plated via 1.4/0.6 mm [package=THT]
  VIA_COIL_FAN = Plated via 1.4/0.6 mm [package=THT]
  VIA_COIL_FAN_2 = Plated via 1.4/0.6 mm [package=THT]
  VIA_COIL_HEAT = Plated via 1.4/0.6 mm [package=THT]
  VIA_DWIN_TX = Plated via 1.4/0.6 mm [package=THT]
  VIA_DWIN_TX_2 = Plated via 1.4/0.6 mm [package=THT]
  VIA_DWIN_RX = Plated via 1.4/0.6 mm [package=THT]
  VIA_DWIN_RX_2 = Plated via 1.4/0.6 mm [package=THT]
  VIA_D3_RXD = Plated via 1.4/0.6 mm [package=THT]
  VIA_D7_COMP = Plated via 1.4/0.6 mm [package=THT]
  VIA_D7_COMP_2 = Plated via 1.4/0.6 mm [package=THT]
  VIA_D6_FAN = Plated via 1.4/0.6 mm [package=THT]
  VIA_D6_FAN_2 = Plated via 1.4/0.6 mm [package=THT]
  VIA_D8_HEAT = Plated via 1.4/0.6 mm [package=THT]
  VIA_D8_HEAT_2 = Plated via 1.4/0.6 mm [package=THT]
  VIA_D8_HEAT_3 = Plated via 1.4/0.6 mm [package=THT]
  VIA_D8_HEAT_4 = Plated via 1.4/0.6 mm [package=THT]

nets:
  L_IN: J20.L, F2.2
  OUT_HEAT: J20.CALOR, RL3.NO, RL3.NO'
  OUT_FAN: J20.VENT, RL2.NO, RL2.NO'
  OUT_COMP: J20.COMP, RL1.NO, RL1.NO'
  L_FUSED: F2.1, RL1.COM, RL1.COM', RL2.COM, RL2.COM', RL3.COM, RL3.COM'
  +5V: RL1.A1, RL2.A1, RL3.A1, U1.T00_VIN, J6.1, J6.2, J6.F5V, D1.K, D2.K, D3.K, F1.2, C1.+, C2.1
  COIL_COMP: RL1.A2, Q1.C, D1.A, VIA_COIL_COMP.via
  N1: RL1.NC, RL1.NC'
  COIL_FAN: RL2.A2, Q2.C, D2.A, VIA_COIL_FAN.via, VIA_COIL_FAN_2.via
  N2: RL2.NC, RL2.NC'
  COIL_HEAT: RL3.A2, Q3.C, D3.A, VIA_COIL_HEAT.via
  N3: RL3.NC, RL3.NC'
  GND: U1.T01_GND, U1.B08_GND, J6.3, J6.4, J6.5, J6.FGND, R2.2, Q1.E, R4.2, Q2.E, R6.2, Q3.E, J1.GND, C1.-, C2.2, J5.GND, J3.GND, C3.2, VIA_GND.via, VIA_GND_2.via
  D8_HEAT: U1.B04_D8, R5.1, VIA_D8_HEAT.via, VIA_D8_HEAT_2.via, VIA_D8_HEAT_3.via, VIA_D8_HEAT_4.via
  D7_COMP: U1.B05_D7, R1.1, VIA_D7_COMP.via, VIA_D7_COMP_2.via
  D6_FAN: U1.B06_D6, R3.1, VIA_D6_FAN.via, VIA_D6_FAN_2.via
  +3V3: U1.B09_3V3, J5.3V3, J3.3V3, C3.1, R16.2, R17.2
  D4_TXD: U1.B10_D4, R17.1, R19.1
  D3_RXD: U1.B11_D3, R16.1, R18.1, VIA_D3_RXD.via
  D2_SDA: U1.B12_D2, J5.SDA, J3.SDA
  D1_SCL: U1.B13_D1, J5.SCL, J3.SCL
  DWIN_TX: J6.49, J6.FTX, R18.2, VIA_DWIN_TX.via, VIA_DWIN_TX_2.via
  DWIN_RX: J6.50, J6.FRX, R19.2, VIA_DWIN_RX.via, VIA_DWIN_RX_2.via
  BASE_COMP: R1.2, R2.1, Q1.B
  BASE_FAN: R3.2, R4.1, Q2.B
  BASE_HEAT: R5.2, R6.1, Q3.B
  +5V_IN: J1.+5V, F1.1

custom parts:
  Screw terminal 4P 5.08 mm: Phoenix MKDS 1,5 family, 1.30 mm drill
  TR5 fuse 5.08 mm: Radial TR5 fuse, 8.5 mm body
  Hongfa HF115F/005-1ZS3 (16 A, 5 mm pinning): SPDT 16 A 250 VAC relay, 5 V coil, 29 x 12.7 x 15.7 mm
  NodeMCU Amica v2 socket (22.86 mm rows): Two 1x15 female headers, rows 0.9 in apart (NodeMCU Amica / v2, 48 x 25.4 mm)
  FPC 0.5 mm 50P upper contact (AFC07-S50ECA-00), bottom side: JUSHUO AFC07-S50ECA-00, slide lock, H 2.0 mm; mounted on the bottom side
  0805 res: SMD 0805
  0805 res: SMD 0805
  BC817-40 SOT-23 (1=B 2=E 3=C): SOT-23 NPN
  1N4148W SOD-123 (cathode bar = pad 1): SOD-123 diode
  Screw terminal 2P 5.08 mm: Phoenix MKDS 1,5 family, 1.30 mm drill
  PTC 1812: SMD 1812 polyfuse
  Electrolytic 6.3 mm, 2.5 mm pitch: Radial electrolytic
  0805 cap: SMD 0805
  JST XH 4P B4B-XH-A: JST XH top entry, 2.50 mm, 0.90 mm drill
  0805 res: SMD 0805
  Mounting hole NPTH 3.2 mm: Unplated mounting hole; use nylon M3 screws.
  Rev B board legend: Board-level silkscreen legend.
  Plated via 1.4/0.6 mm: Two-layer plated through via.
